# Fritzing sketch Voice Assistant W48 verkürzte Kabelwege (saved by Fritzing 1.0.4)
breadboards: 1

parts:
  A1 = ESP32-S3-WROOM-1-N16R8 dev board
  R2 = Resistor [tolerance=±1% power=0.25W resistance=20 package=THT]
  R3 = Resistor [tolerance=±1% power=0.25W resistance=20 package=THT]
  LED1 = LED - 3mm [color="Green (570nm)" current=20mA package="3 mm [THT]"]
  LED2 = LED - 3mm [color="Red (660nm)" current=20mA package="3 mm [THT]"]
  Mic = INMP441
  AMP = Adafruit MAX98357A I2S 3W Class D Amplifier [part_number="Adafruit #3006"]
  Speaker = Piezo Speaker
  Switch_(Handset) = SWITCH-MOMENTARY-2 [package=tactile-switch-1101ne]

nets:
  N1: A1.Pin_1, A1.Pin_2, R2.Pin_0, R3.Pin_0, Mic.VDD, Switch_(Handset).1
  N2: A1.Pin_9, Mic.SCK, AMP.BCLK
  N3: A1.Pin_10, Mic.WS, AMP.LRCLK
  N4: A1.Pin_15, AMP.DIN
  N5: A1.Pin_19, Mic.SD
  N6: A1.Pin_21, AMP.VIN
  GND: A1.Pin_22, Mic.L/R, Mic.GND, AMP.GND
  N7: A1.Pin_37, Switch_(Handset).2
  N8: A1.Pin_38, LED2.cathode
  N9: A1.Pin_39, LED1.cathode
  N10: R2.Pin_1, LED1.anode
  N11: R3.Pin_1, LED2.anode
  N12: AMP.VO-, Speaker.pin1
  N13: AMP.VO+, Speaker.pin2

custom parts:
  ESP32-S3-WROOM-1-N16R8 dev board: ESP32-S3 WIFI+BLE5.0 Development Board ESP32-S3-WROOM-1-N16R8(16M Flash/8SRAM).
  INMP441: This is a simple breakout board for the INMP441 I2S MEMS microphone.
  Adafruit MAX98357A I2S 3W Class D Amplifier: Listen to this good news - we now have an all in one digital audio amp breakout board that works incredibly well with the Raspberry Pi! If you're looking for an easy and low cost way to get you digital sound files bumpin' then the MAX08357 I2S Amp Breakout is for you. It takes standard I2S digital audio input and, not only decodes it into analog, but also amplifies it directly into a speaker.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
